# Fritzing sketch rf_transciever (saved by Fritzing 0.9.2b)
breadboards: 1

parts:
  Part1 = Arduino Uno (Rev3)
  Part2 = Arduino Uno (Rev3)
  U1 = RF-LINK_TX [package=rf-link_tx]
  U2 = RF-LINK_RX [package=rf-link_rx]

nets:
  N1: Part1.D1/TX, U1.GND
  5V: Part1.5V, U1.+5V
  N2: Part1.GND, U1.ANT
  N3: Part2.D0/RX, U2.ANT
